# Fritzing sketch Colour Word Clock PCBV08-HC-12-DCF77 (saved by Fritzing 0.9.4)
circuit board: 9cm x 6cm

parts:
  Bluetooth/HC-12 = male pin header, 6 pins [form="♂ (male)"]
  RTC-clock = female pin header, 6 pins [form="♀ (female)"]
  R16 = Resistor [tolerance=±5% resistance=1.1k package=THT]
  R17 = Resistor [tolerance=±5% resistance=2.2k package=THT]
  DCF = female pin header, 3 pins [form="♀ (female)"]
  J1 = Screw terminal - 2 pins [package=THT]
  R18 = Resistor [tolerance=±5% resistance=470 package=THT]
  R19 = Resistor [tolerance=±5% resistance=470 package=THT]
  - = LED - 3mm [color="Red (633nm)" package="3 mm [THT]"]
  -_2 = LED - 3mm [color="Yellow (592nm)" package="3 mm [THT]"]
  Nano_Every = Arduino Nano (Rev3.0) (ICSP)

nets:
  N1: Bluetooth/HC-12.pin2, R16.Pin_1, R17.Pin_0
  N2: Bluetooth/HC-12.pin3, Nano_Every.D7
  N3: Bluetooth/HC-12.pin4, R17.Pin_1, -.cathode, -_2.cathode
  N4: Bluetooth/HC-12.pin5, RTC-clock.pin2, DCF.pin1, J1.pin2, Nano_Every.5V
  N5: RTC-clock.pin1, DCF.pin3, J1.pin1, Nano_Every.GND
  N6: RTC-clock.pin3, Nano_Every.A4
  N7: RTC-clock.pin4, Nano_Every.A5
  N8: R16.Pin_0, Nano_Every.D6
  N9: R18.Pin_0, -.anode
  N10: R18.Pin_1, Nano_Every.D10
  N11: R19.Pin_0, Nano_Every.D9
  N12: R19.Pin_1, -_2.anode

notes:
  Gnd
  32K
  SQW
  SCL
  SDA
  5V
  State
  <-RX
  TX->
  EN
  Power
  RX
  TX
  A5
  A4
  D5
  -
  +
  Signal
  DCF
  A3
  A2
  D9
  D10
